# Fritzing sketch schema_fritzing_allimentation_stabilisé (saved by Fritzing 0.9.3b)
breadboards: 1

parts:
  C1 = Electrolytic Capacitor [capacitance=1000μF package="1010 [SMD, electrolytic]"]
  C2 = Capacitor [package=cap-pth-small2]
  U1 = Voltage Regulator [package=to220-adj]
  R1 = Trimmer Potentiometer [maximum_resistance=10kΩ package=THT]
  R2 = Resistor [tolerance=±5% resistance=220 package="2512 [SMD]"]
  C3 = Electrolytic Capacitor [capacitance=100µF package="200 mil [THT, electrolytic]"]

nets:
  N1: C1.-, C2.1, R1.wiper
  N2: C1.+, C2.2, R1.leg1, C3.+
  N3: U1.ADJ, R1.leg2
  N4: U1.IN, R2.Pin_0
  N5: U1.OUT, R2.Pin_1, C3.-
