# Fritzing sketch DETECTEUR_RADAR (saved by Fritzing 0.9.6b)
breadboards: 1

parts:
  Composant1 = Arduino Uno (Rev3)
  J1 = Piezo Speaker
  R1 = Resistor [tolerance=±5% power=0.25 resistance=220 package=THT]
  HC-SR04_Sensor_1 = HC-SR04 Ultrasonic Distance Sensor
  M1 = Dagu DGServo 9g (Top view) [part_number=RS001B]
  U1 = LCD-16X2 [package=lcd-16x2_noholes]
  R2 = Resistor [tolerance=±5% power=0.25 resistance=220 package=THT]
  R4 = Trimmer Potentiometer [maximum_resistance=10kΩ package=THT]
  LED1 = smd LED [color="Red (633nm)" package="1206 [SMD]"]
  R5 = Resistor [tolerance=±5% power=0.25 resistance=220 package=THT]

nets:
  N1: Composant1.D8, M1.pulse
  N2: Composant1.D10_PWM/SS, R5.Pin_1
  N3: Composant1.D11_PWM/MOSI, U1.E
  N4: Composant1.D12/MISO, U1.RS
  N5: Composant1.D13/SCK, R1.Pin_1
  GND: Composant1.GND, J1.pin1, HC-SR04_Sensor_1.GND, M1.gnd, U1.VSS, U1.R_W, U1.K, R4.wiper, LED1.cathode
  N6: Composant1.D2, U1.DB7
  N7: Composant1.D3_PWM, U1.DB6
  N8: Composant1.D4, U1.DB5
  N9: Composant1.D5_PWM, U1.DB4
  N10: Composant1.D6_PWM, HC-SR04_Sensor_1.ECHO
  N11: Composant1.D7, HC-SR04_Sensor_1.TRIG
  VCC: Composant1.5V, HC-SR04_Sensor_1.VCC, M1.vcc, U1.VDD, R2.Pin_0
  N12: J1.pin2, R1.Pin_0
  N13: U1.VO, R4.leg1
  N14: LED1.anode, R5.Pin_0
